# Fritzing sketch StatusDisplay (saved by Fritzing 0.9.2b)
breadboards: 1

parts:
  U1 = atmega328 [package=dip]
  S1 = Pushbutton [package="[THT]"]
  C1 = Ceramic Capacitor [capacitance=100nF package="100 mil [THT, multilayer]"]
  XTAL1 = CRYSTAL - kHz [frequency="16 MHz"]
  C2 = Ceramic Capacitor [capacitance=100nF package="100 mil [THT, multilayer]"]
  C3 = Ceramic Capacitor [capacitance=100nF package="100 mil [THT, multilayer]"]
  R1 = Resistor [tolerance=±5% resistance=330 package=THT]
  R2 = Resistor [tolerance=±5% resistance=1k package=THT]
  LED1 = LED - 3mm [color="Red (633nm)" package="3 mm [THT]"]
  부품1 = LED Matrix - Serial Interface - Red/Green/Blue
  BLUEFRUIT1 = Adafruit Bluefruit EZ-LINK v1.0
  R3 = Resistor [tolerance=±5% resistance=330 package=THT]
  LED2 = LED - 3mm [color="Green (570nm)" package="3 mm [THT]"]

nets:
  N1: U1.RESET, S1.Pin_1, S1.Pin_2, R2.Pin_0
  VCC: U1.VCC, U1.AVCC, U1.AREF, C1.0, R1.Pin_1, R2.Pin_1, 부품1.VCC, BLUEFRUIT1.Vin
  GND: U1.GND, S1.Pin_3, S1.Pin_4, C1.1, C2.1, C3.1, LED1.anode, 부품1.GND, BLUEFRUIT1.GND, R3.Pin_0
  N2: U1.XLAT1, XTAL1.pin_0, C2.0
  N3: U1.XLAT2, XTAL1.pin_1, C3.0
  N4: U1.D8, BLUEFRUIT1.TX
  N5: U1.D9_(PWM), BLUEFRUIT1.RX
  N6: U1.D10_(PWM), 부품1.SCK
  N7: U1.D11_(PWM), 부품1.CS
  N8: U1.D12, 부품1.MOSI
  N9: U1.D13, LED2.cathode
  N10: R1.Pin_0, LED1.cathode
  N11: R3.Pin_1, LED2.anode

custom parts:
  Adafruit Bluefruit EZ-LINK v1.0: Bluefruit EZ-LINK, Bluetooth Serial Link & Arduino Programmer
